# Fritzing sketch brain_schematic (saved by Fritzing 0.9.3b)
breadboards: 1

parts:
  R1 = Resistor [tolerance=±5% resistance=2.2k package="1206 [SMD]"]
  R2 = Resistor [tolerance=±5% resistance=3.3k package="0805 [SMD]"]
  M1 = DC Motor
  U1 = TRANSISTOR_NPN_2 [package=to-92]
  R3 = Resistor [tolerance=±5% resistance=220 package="1206 [SMD]"]
  D1 = P1000K [part_number=P1000K]  # not connected

nets:
  N1: R1.Pin_1, R2.Pin_1
  N2: M1.pin_2, U1.E
  N3: U1.B, R3.Pin_1

notes:
  the yellow line: TX(mindflex)--->pin10 (Arduino)
  the black line: GND (mindflex) to the GND (Arduino)
  Yellow line: mindflex(TX)---> bluetooth(RX)
  green line: mindflex(RX)-->bluetoooth(TX)
  red line: 3.3V
  black line: GND
  yellow line: bluetooth(RX)-->Arduino(Rx)
  green line: bluetooth(TX)-->Arduino(Tx)
  red line: bluetooth(VCC)-->Arduino(5V)
  Black line: bluetooth(GND)-->Arduino(GND)
  orange line: bluetooth(EN)-->Arduino(3.3V)
